# Fritzing sketch PCB (saved by Fritzing 0.9.3b)
perfboards: 2

parts:
  Part1 = Arduino Pro Mini v13
  S1 = Pushbutton [package="[THT]"]
  S2 = Pushbutton [package="[THT]"]
  U1 = TEMPERATURE-SENSOR [package=to-92]
  LED1 = LED - 5mm [color="Green (555nm)" package="5 mm [THT]"]
  LED2 = LED - 5mm [color="Red (633nm)" package="5 mm [THT]"]
  R4 = Resistor [tolerance=±5% resistance=220 package=THT]
  R5 = Resistor [tolerance=±5% resistance=220 package=THT]
  R1 = Rotary Potentiometer (Small) [maximum_resistance=100kΩ package=THT]
  IC1 = MICROCONTROLLER [package=dil28-3-zif_socket]  # not connected

nets:
  N1: Part1.A3, S2.Pin_3, S2.Pin_4
  N2: Part1.A2, U1.ADJ
  N3: Part1.A1, S1.Pin_3, S1.Pin_4
  N4: Part1.A0, R1.wiper
  N5: Part1.D10_PWM/SS, LED1.anode
  N6: Part1.D9_PWM, LED2.anode
  N7: S1.Pin_1, S1.Pin_2
  N8: S2.Pin_1, S2.Pin_2
  N9: LED1.cathode, R5.Pin_1
  N10: LED2.cathode, R4.Pin_1
